# Fritzing sketch AK2_C04_L14_Accurate_Alarm_Clock_LCDI2C20x4 (saved by Fritzing 0.9.10b)
breadboards: 1

parts:
  LCD2004-I2C1 = LCD2004-I2C
  Part1 = Arduino Mega 2560 (Rev3)
  Keypad4x1 = Keypad Membran 4x4
  ZS-042_RTC1 = ZS-042 RTC Module
  J1 = Piezo Speaker

nets:
  GND: LCD2004-I2C1.GND, Part1.GND, ZS-042_RTC1.GND, J1.pin1
  VCC: LCD2004-I2C1.VCC, Part1.5V, ZS-042_RTC1.VCC
  N1: LCD2004-I2C1.SDA, Part1.D20/SDA, ZS-042_RTC1.SDA
  N2: LCD2004-I2C1.SCL, Part1.D21/SCL, ZS-042_RTC1.SCL
  N3: Part1.D23, Keypad4x1.Pin1
  N4: Part1.D25, Keypad4x1.Pin2
  N5: Part1.D27, Keypad4x1.Pin3
  N6: Part1.D29, Keypad4x1.Pin4
  N7: Part1.D31, Keypad4x1.Pin5
  N8: Part1.D33, Keypad4x1.Pin6
  N9: Part1.D35, Keypad4x1.Pin7
  N10: Part1.D37, Keypad4x1.Pin8
  N11: Part1.D47, J1.pin2

custom parts:
  LCD2004-I2C: A standard character display with 4x20 characters. Comes in many colors with LCM2004 IIC attached.
  Keypad Membran 4x4: Membrane Keypad 4x4 Matrix
